// Logisim project LC3-2200b HUA JIAN.circ as structural Verilog
module main (
  output [31:0] out_1,
  output [31:0] out_2,
  output [31:0] out_3,
  output [31:0] out_4,
  output [31:0] out_5,
  output [31:0] out_6,
  output [31:0] out_7,
  output [3:0] out_8,
  output [31:0] out_9
);

  wire BEQ, CLK, comparator_1_eq, comparator_2_eq, comparator_3_eq, comparator_5_eq, comparator_6_eq,
       comparator_7_eq, comparator_8_eq, comparator_9_eq, comparator_10_eq, comparator_11_eq,
       comparator_12_eq, comparator_13_eq, comparator_14_eq, comparator_15_eq, comparator_16_eq,
       comparator_17_eq, comparator_18_eq, comparator_19_eq, comparator_20_eq, ENGB1, ENGB2, ENGB3, JALR,
       multiplexer_9_out, NOOPB2, NOOPB3, NOOPB4, not_1_out, not_2_out, not_3_out, not_6_out, or_1_out,
       or_2_out, or_3_out, or_4_out, or_5_out, or_7_out, or_8_out, or_9_out, STOPPC, WREN;
  wire [3:0] BS, buffer_2_opcode, buffer_2_rxs, buffer_3_opcode, buffer_3_rxs, buffer_4_opcode, rom_1_data;
  wire [31:0] adder_1_out, alu_1_out, bit_extender_1_out, buffer_2_rz_2, buffer_3_pc_2, buffer_4_in_2,
       buffer_4_pc_2, dual_ported_register_file_1_out1, dual_ported_register_file_1_out2, EXPC,
       multiplexer_1_out, multiplexer_2_out, multiplexer_3_out, multiplexer_4_out, multiplexer_6_out,
       multiplexer_7_out, multiplexer_10_out, ram_1_data, ram_2_data, register_1_q;

  Multiplexer #(.width(32), .disabled(0), .enable("false")) multiplexer_1 (
    .in0(multiplexer_3_out), .in1(EXPC), .out(multiplexer_1_out), .sel(JALR));
  Multiplexer #(.width(32), .disabled(0), .enable("false")) multiplexer_2 (
    .in0(multiplexer_1_out), .in1(register_1_q), .out(multiplexer_2_out), .sel(STOPPC));
  Register #(.width(32)) register_1 (.D(multiplexer_2_out), .en(not_1_out), .Q(register_1_q), .clk(CLK));  // open: clr
  not not_1 (not_1_out, comparator_1_eq);
  Multiplexer #(.width(32), .disabled(0), .enable("false")) multiplexer_3 (
    .in0(adder_1_out), .in1(out_7), .out(multiplexer_3_out), .sel(BEQ));
  Adder #(.width(32)) adder_1 (.a(register_1_q), .b(32'h1), .out(adder_1_out));  // open: cin, cout
  Multiplexer #(.width(32), .disabled(0), .enable("false")) multiplexer_4 (
    .in0(ram_1_data), .in1(32'hf0000000), .out(multiplexer_4_out), .sel(comparator_1_eq));
  RAM #(.addrWidth(24), .dataWidth(32)) ram_1 (
    .addr(register_1_q[23:0]), .data(ram_1_data));  // open: sel, clk, ld, clr
  or or_1 (or_1_out, JALR, BEQ);
  BUFFER buffer_1 (
    .PC(adder_1_out), .IN(multiplexer_4_out), .CLK(CLK), .PC_2(out_1), .IN_2(out_5), .in_1(or_1_out),
    .ENG(ENGB1));  // open: RX, RYS, RY, RZS, RZ, OFF, OPCODE, RXS, RX_2, RYS_2, RY_2, RZS_2, RZ_2, OFF_2, in_4, in_5
  Comparator #(.width(4), .mode("unsigned")) comparator_1 (
    .a(4'b1111), .b(out_5[31:28]), .eq(comparator_1_eq));  // open: gt, lt
  Clock clock_1 (.out(CLK));
  Comparator #(.width(4), .mode("unsigned")) comparator_2 (
    .a(out_5[31:28]), .b(4'b0011), .eq(comparator_2_eq));  // open: gt, lt
  Comparator #(.width(4), .mode("unsigned")) comparator_3 (
    .a(out_5[31:28]), .b(4'b0111), .eq(comparator_3_eq));  // open: gt, lt
  Multiplexer #(.width(4), .disabled(0), .enable("false")) multiplexer_5 (
    .in0({out_5[0], out_5[1], out_5[2], out_5[3]}), .in1(out_5[27:24]), .out(BS), .sel(or_2_out));
  or or_2 (or_2_out, comparator_2_eq, comparator_3_eq);
  assign bit_extender_1_out = {{12{out_5[19]}}, out_5[19:0]};  // Bit_Extender bit_extender_1
  Dual_Ported_Register_File dual_ported_register_file_1 (
    .CLK(CLK), .WrREGNO(out_8), .RdREGNO1(out_5[23:20]), .RdREGNO2(BS), .INPUT(out_4),
    .OUT1(dual_ported_register_file_1_out1), .OUT2(dual_ported_register_file_1_out2), .WrEN(WREN));
  or or_3 (or_3_out, NOOPB2, or_1_out);
  BUFFER buffer_2 (
    .PC(out_1), .RYS(out_5[23:20]), .RY(dual_ported_register_file_1_out1),
    .RZS({out_5[0], out_5[1], out_5[2], out_5[3]}), .RZ(dual_ported_register_file_1_out2),
    .OFF(bit_extender_1_out), .CLK(CLK), .PC_2(out_2), .OPCODE(buffer_2_opcode), .RXS(buffer_2_rxs),
    .RY_2(EXPC), .RZ_2(buffer_2_rz_2), .OFF_2(out_6), .in_4(out_5[31:28]), .in_5(out_5[27:24]),
    .in_1(or_3_out), .ENG(ENGB2));  // open: IN, RX, IN_2, RX_2, RYS_2, RZS_2
  Comparator #(.width(4), .mode("unsigned")) comparator_4 (
    .a(buffer_2_opcode), .b(4'b0100), .eq(JALR));  // open: gt, lt
  Adder #(.width(32)) adder_2 (.a(out_2), .b(out_6), .out(out_7));  // open: cin, cout
  Multiplexer #(.width(32), .disabled(0), .enable("false")) multiplexer_6 (
    .in0(buffer_2_rz_2), .in1(out_6), .out(multiplexer_6_out), .sel(rom_1_data[2]));
  ROM #(.addrWidth(4), .dataWidth(4)) rom_1 (.addr(buffer_2_opcode), .data(rom_1_data));  // open: sel
  Multiplexer #(.width(32), .disabled(0), .enable("false")) multiplexer_7 (
    .in0(alu_1_out), .in1(out_2), .out(multiplexer_7_out), .sel(JALR));
  ALU alu_1 (.A(EXPC), .B(multiplexer_6_out), .FUN(rom_1_data[1:0]), .OUT(alu_1_out));
  Multiplexer #(.disabled(0), .enable("false")) multiplexer_8 (
    .in0(1'b0), .in1(comparator_5_eq), .out(BEQ), .sel(rom_1_data[3]));
  Comparator #(.width(32), .mode("unsigned")) comparator_5 (
    .a(alu_1_out), .b({32{1'b0}}), .eq(comparator_5_eq));  // open: gt, lt
  Comparator #(.width(4), .mode("unsigned")) comparator_6 (
    .a(buffer_2_rxs), .b(out_5[23:20]), .eq(comparator_6_eq));  // open: gt, lt
  Comparator #(.width(4), .mode("unsigned")) comparator_7 (
    .a(buffer_2_rxs), .b(BS), .eq(comparator_7_eq));  // open: gt, lt
  BUFFER buffer_3 (
    .PC(out_7), .IN(multiplexer_7_out), .RX(buffer_2_rz_2), .CLK(CLK), .PC_2(buffer_3_pc_2), .IN_2(out_3),
    .OPCODE(buffer_3_opcode), .RXS(buffer_3_rxs), .RX_2(out_9), .in_4(buffer_2_opcode), .in_5(buffer_2_rxs),
    .in_1(NOOPB3), .ENG(ENGB3));  // open: RYS, RY, RZS, RZ, OFF, RYS_2, RY_2, RZS_2, RZ_2, OFF_2
  Comparator #(.width(4), .mode("unsigned")) comparator_8 (
    .a(buffer_2_rxs), .b(4'b0000), .eq(comparator_8_eq));  // open: gt, lt
  Comparator #(.width(4), .mode("unsigned")) comparator_9 (
    .a(buffer_3_opcode), .b(4'b0111), .eq(comparator_9_eq));  // open: gt, lt
  not not_2 (not_2_out, comparator_8_eq);
  or or_4 (or_4_out, comparator_6_eq, comparator_7_eq);
  and and_1 (NOOPB2, not_2_out, or_4_out);
  Comparator #(.width(4), .mode("unsigned")) comparator_10 (
    .a(4'b0101), .b(buffer_3_opcode), .eq(comparator_10_eq));  // open: gt, lt
  Multiplexer #(.disabled(0), .enable("false")) multiplexer_9 (
    .in0(1'b0), .in1(1'b1), .out(multiplexer_9_out), .sel(comparator_9_eq));
  RAM #(.addrWidth(24), .dataWidth(32), .bus("separate")) ram_2 (
    .addr(out_3[23:0]), .din(out_9), .data(ram_2_data), .str(multiplexer_9_out), .clk(CLK));  // open: sel, ld, clr
  Comparator #(.width(4), .mode("unsigned")) comparator_11 (
    .a(buffer_3_rxs), .b(out_5[23:20]), .eq(comparator_11_eq));  // open: gt, lt
  Comparator #(.width(4), .mode("unsigned")) comparator_12 (
    .a(buffer_3_rxs), .b(BS), .eq(comparator_12_eq));  // open: gt, lt
  Comparator #(.width(4), .mode("unsigned")) comparator_13 (
    .a(buffer_3_rxs), .b(4'b0000), .eq(comparator_13_eq));  // open: gt, lt
  Multiplexer #(.width(32), .disabled(0), .enable("false")) multiplexer_10 (
    .in0(out_3), .in1(ram_2_data), .out(multiplexer_10_out), .sel(comparator_10_eq));
  not not_3 (not_3_out, comparator_13_eq);
  or or_5 (or_5_out, comparator_11_eq, comparator_12_eq);
  BUFFER buffer_4 (
    .PC(buffer_3_pc_2), .IN(multiplexer_10_out), .CLK(CLK), .PC_2(buffer_4_pc_2), .IN_2(buffer_4_in_2),
    .OPCODE(buffer_4_opcode), .RXS(out_8), .in_4(buffer_3_opcode), .in_5(buffer_3_rxs), .in_1(NOOPB4),
    .ENG(1'b1));  // open: RX, RYS, RY, RZS, RZ, OFF, RX_2, RYS_2, RY_2, RZS_2, RZ_2, OFF_2
  Multiplexer #(.width(32), .disabled(0), .enable("false")) multiplexer_11 (
    .in0(buffer_4_in_2), .in1(buffer_4_pc_2), .out(out_4), .sel(comparator_14_eq));
  and and_2 (NOOPB3, not_3_out, or_5_out);
  or or_6 (STOPPC, NOOPB2, NOOPB3, NOOPB4);
  Comparator #(.width(4), .mode("unsigned")) comparator_14 (
    .a(4'b0110), .b(buffer_4_opcode), .eq(comparator_14_eq));  // open: gt, lt
  not not_4 (ENGB1, STOPPC);
  Comparator #(.width(4), .mode("unsigned")) comparator_15 (
    .a(buffer_4_opcode), .b(4'b0011), .eq(comparator_15_eq));  // open: gt, lt
  Comparator #(.width(4), .mode("unsigned")) comparator_16 (
    .a(buffer_4_opcode), .b(4'b0111), .eq(comparator_16_eq));  // open: gt, lt
  Comparator #(.width(4), .mode("unsigned")) comparator_17 (
    .a(buffer_4_opcode), .b(4'b1111), .eq(comparator_17_eq));  // open: gt, lt
  Comparator #(.width(4), .mode("unsigned")) comparator_18 (
    .a(out_8), .b(out_5[23:20]), .eq(comparator_18_eq));  // open: gt, lt
  Comparator #(.width(4), .mode("unsigned")) comparator_19 (.a(out_8), .b(BS), .eq(comparator_19_eq));  // open: gt, lt
  or or_7 (or_7_out, comparator_15_eq, comparator_16_eq, comparator_17_eq);
  Comparator #(.width(4), .mode("unsigned")) comparator_20 (
    .a(out_8), .b(4'b0000), .eq(comparator_20_eq));  // open: gt, lt
  or or_8 (or_8_out, NOOPB3, NOOPB4);
  not not_5 (ENGB2, or_8_out);
  Multiplexer #(.disabled(0), .enable("false")) multiplexer_12 (.in0(1'b1), .in1(1'b0), .out(WREN), .sel(or_7_out));
  not not_6 (not_6_out, comparator_20_eq);
  or or_9 (or_9_out, comparator_18_eq, comparator_19_eq);
  and and_3 (NOOPB4, not_6_out, or_9_out);
  not not_7 (ENGB3, NOOPB4);

  // Other names for the same wires on the sheet: AS[3:0] = out_5[23:20]; WR[3:0] = out_8; WRDATA[31:0] = out_4

  // Notes on the sheet:
  //   contents of rom_1 (hex, n*v repeats v):
  //   0 4 1 a 0 4 0 4
endmodule

module Dual_Ported_Register_File (
  input  CLK,
  input  WrEN,
  input  [3:0] WrREGNO,
  input  [3:0] RdREGNO1,
  input  [3:0] RdREGNO2,
  input  [31:0] INPUT,
  output [31:0] OUT1,
  output [31:0] OUT2
);

  wire En_a0, En_a1, En_a2, En_at, En_fp, En_k0, En_ra, En_s0, En_s1, En_s2, En_sp, En_t0, En_t1, En_t2,
       En_v0;
  wire [31:0] a0, a1, a2, at, fp, k0, ra, s0, s1, s2, sp, t0, t1, t2, v0, zero;

  Decoder #(.select(4), .disabled(0)) decoder_1 (
    .out1(En_at), .out2(En_v0), .out3(En_a0), .out4(En_a1), .out5(En_a2), .out6(En_t0), .out7(En_t1),
    .out8(En_t2), .out9(En_s0), .out10(En_s1), .out11(En_s2), .out12(En_k0), .out13(En_sp), .out14(En_fp),
    .out15(En_ra), .sel(WrREGNO), .en(WrEN));  // open: out0
  Register #(.width(32)) u_zero (.D(INPUT), .en(1'b0), .Q(zero), .clk(CLK));  // open: clr
  Register #(.width(32)) u_at (.D(INPUT), .en(En_at), .Q(at), .clk(CLK));  // open: clr
  Register #(.width(32)) u_v0 (.D(INPUT), .en(En_v0), .Q(v0), .clk(CLK));  // open: clr
  Register #(.width(32)) u_a0 (.D(INPUT), .en(En_a0), .Q(a0), .clk(CLK));  // open: clr
  Register #(.width(32)) u_a1 (.D(INPUT), .en(En_a1), .Q(a1), .clk(CLK));  // open: clr
  Register #(.width(32)) u_a2 (.D(INPUT), .en(En_a2), .Q(a2), .clk(CLK));  // open: clr
  Register #(.width(32)) u_t0 (.D(INPUT), .en(En_t0), .Q(t0), .clk(CLK));  // open: clr
  Register #(.width(32)) u_t1 (.D(INPUT), .en(En_t1), .Q(t1), .clk(CLK));  // open: clr
  Multiplexer #(.select(4), .width(32), .disabled(0), .enable("false")) multiplexer_1 (
    .in0(zero), .in1(at), .in2(v0), .in3(a0), .in4(a1), .in5(a2), .in6(t0), .in7(t1), .in8(t2), .in9(s0),
    .in10(s1), .in11(s2), .in12(k0), .in13(sp), .in14(fp), .in15(ra), .out(OUT2), .sel(RdREGNO2));
  Register #(.width(32)) u_t2 (.D(INPUT), .en(En_t2), .Q(t2), .clk(CLK));  // open: clr
  Register #(.width(32)) u_s0 (.D(INPUT), .en(En_s0), .Q(s0), .clk(CLK));  // open: clr
  Register #(.width(32)) u_s1 (.D(INPUT), .en(En_s1), .Q(s1), .clk(CLK));  // open: clr
  Register #(.width(32)) u_s2 (.D(INPUT), .en(En_s2), .Q(s2), .clk(CLK));  // open: clr
  Register #(.width(32)) u_k0 (.D(INPUT), .en(En_k0), .Q(k0), .clk(CLK));  // open: clr
  Register #(.width(32)) u_sp (.D(INPUT), .en(En_sp), .Q(sp), .clk(CLK));  // open: clr
  Register #(.width(32)) u_fp (.D(INPUT), .en(En_fp), .Q(fp), .clk(CLK));  // open: clr
  Register #(.width(32)) u_ra (.D(INPUT), .en(En_ra), .Q(ra), .clk(CLK));  // open: clr
  Multiplexer #(.select(4), .width(32), .disabled(0), .enable("false")) multiplexer_2 (
    .in0(zero), .in1(at), .in2(v0), .in3(a0), .in4(a1), .in5(a2), .in6(t0), .in7(t1), .in8(t2), .in9(s0),
    .in10(s1), .in11(s2), .in12(k0), .in13(sp), .in14(fp), .in15(ra), .out(OUT1), .sel(RdREGNO1));

  // Notes on the sheet:
  //   MODIFY AT YOUR OWN RISK
endmodule

module BUFFER (
  input  in_1,
  input  [31:0] PC,
  input  [31:0] IN,
  input  [3:0] in_4,
  input  [3:0] in_5,
  input  [31:0] RX,
  input  [3:0] RYS,
  input  [31:0] RY,
  input  [3:0] RZS,
  input  [31:0] RZ,
  input  [31:0] OFF,
  input  CLK,
  input  ENG,
  output [31:0] PC_2,
  output [31:0] IN_2,
  output [3:0] OPCODE,
  output [3:0] RXS,
  output [31:0] RX_2,
  output [3:0] RYS_2,
  output [31:0] RY_2,
  output [3:0] RZS_2,
  output [31:0] RZ_2,
  output [31:0] OFF_2
);

  wire [3:0] multiplexer_4_out, multiplexer_6_out, multiplexer_9_out, multiplexer_10_out;
  wire [31:0] multiplexer_1_out, multiplexer_2_out, multiplexer_3_out, multiplexer_5_out, multiplexer_7_out,
       multiplexer_8_out;

  Multiplexer #(.width(32), .disabled(0), .enable("false")) multiplexer_1 (
    .in0(PC), .in1({32{1'b0}}), .out(multiplexer_1_out), .sel(in_1));
  Multiplexer #(.width(32), .disabled(0), .enable("false")) multiplexer_2 (
    .in0(IN), .in1({32{1'b0}}), .out(multiplexer_2_out), .sel(in_1));
  Multiplexer #(.width(32), .disabled(0), .enable("false")) multiplexer_3 (
    .in0(RX), .in1({32{1'b0}}), .out(multiplexer_3_out), .sel(in_1));
  Multiplexer #(.width(4), .disabled(0), .enable("false")) multiplexer_4 (
    .in0(RYS), .in1(4'b0000), .out(multiplexer_4_out), .sel(in_1));
  Multiplexer #(.width(32), .disabled(0), .enable("false")) multiplexer_5 (
    .in0(RY), .in1({32{1'b0}}), .out(multiplexer_5_out), .sel(in_1));
  Multiplexer #(.width(4), .disabled(0), .enable("false")) multiplexer_6 (
    .in0(RZS), .in1(4'b0000), .out(multiplexer_6_out), .sel(in_1));
  Multiplexer #(.width(32), .disabled(0), .enable("false")) multiplexer_7 (
    .in0(RZ), .in1({32{1'b0}}), .out(multiplexer_7_out), .sel(in_1));
  Multiplexer #(.width(32), .disabled(0), .enable("false")) multiplexer_8 (
    .in0(OFF), .in1({32{1'b0}}), .out(multiplexer_8_out), .sel(in_1));
  Multiplexer #(.width(4), .disabled(0), .enable("false")) multiplexer_9 (
    .in0(in_4), .in1(4'b0000), .out(multiplexer_9_out), .sel(in_1));
  Multiplexer #(.width(4), .disabled(0), .enable("false")) multiplexer_10 (
    .in0(in_5), .in1(4'b0000), .out(multiplexer_10_out), .sel(in_1));
  Register #(.width(32)) u_PC (.D(multiplexer_1_out), .en(ENG), .Q(PC_2), .clk(CLK));  // open: clr
  Register #(.width(32)) u_IN (.D(multiplexer_2_out), .en(ENG), .Q(IN_2), .clk(CLK));  // open: clr
  Register #(.width(4)) u_OPCODE (.D(multiplexer_9_out), .en(ENG), .Q(OPCODE), .clk(CLK));  // open: clr
  Register #(.width(4)) u_RXS (.D(multiplexer_10_out), .en(ENG), .Q(RXS), .clk(CLK));  // open: clr
  Register #(.width(32)) u_RX (.D(multiplexer_3_out), .en(ENG), .Q(RX_2), .clk(CLK));  // open: clr
  Register #(.width(4)) u_RYS (.D(multiplexer_4_out), .en(ENG), .Q(RYS_2), .clk(CLK));  // open: clr
  Register #(.width(32)) u_RY (.D(multiplexer_5_out), .en(ENG), .Q(RY_2), .clk(CLK));  // open: clr
  Register #(.width(4)) u_RZS (.D(multiplexer_6_out), .en(ENG), .Q(RZS_2), .clk(CLK));  // open: clr
  Register #(.width(32)) u_RZ (.D(multiplexer_7_out), .en(ENG), .Q(RZ_2), .clk(CLK));  // open: clr
  Register #(.width(32)) u_OFF (.D(multiplexer_8_out), .en(ENG), .Q(OFF_2), .clk(CLK));  // open: clr
endmodule

module ALU (
  input  [31:0] A,
  input  [31:0] B,
  input  [1:0] FUN,
  output [31:0] OUT
);

  wire [31:0] adder_1_out, nand_1_out, subtractor_1_out;

  Adder #(.width(32)) adder_1 (.a(A), .b(B), .out(adder_1_out));  // open: cin, cout
  Subtractor #(.width(32)) subtractor_1 (.a(A), .b(B), .out(subtractor_1_out));  // open: bin, bout
  assign nand_1_out = ~(A & B);  // NAND_Gate nand_1, 32 bits wide
  Multiplexer #(.select(2), .width(32), .disabled(0), .enable("false")) multiplexer_1 (
    .in0(adder_1_out), .in1(nand_1_out), .in2(subtractor_1_out), .out(OUT), .sel(FUN));  // open: in3
endmodule
